# Fritzing sketch HangManClient (saved by Fritzing 0.9.3b)
breadboards: 1

parts:
  LCD1 = LCD screen
  Raspberry_Pi_1 = Raspberry Pi 3 [part_number=RPI-3-V1.2]
  R1 = Rotary Potentiometer (Small) [maximum_resistance=100kΩ package=THT]
  R2 = Resistor [tolerance=±5% resistance=220 package="2512 [SMD]"]  # not connected

nets:
  VSS: LCD1.VSS, LCD1.LED-, Raspberry_Pi_1.GND, R1.leg1
  VDD: LCD1.VDD, Raspberry_Pi_1.5V, R1.leg2
  N1: LCD1.V0, R1.wiper
  N2: LCD1.RS, Raspberry_Pi_1.GPIO20
  N3: LCD1.R/W, Raspberry_Pi_1.GPIO5
  N4: LCD1.E, Raspberry_Pi_1.GPIO16
  N5: LCD1.DB0, Raspberry_Pi_1.GPIO6
  N6: LCD1.DB1, Raspberry_Pi_1.GPIO13
  N7: LCD1.DB2, Raspberry_Pi_1.GPIO19
  N8: LCD1.DB3, Raspberry_Pi_1.GPIO26
  N9: LCD1.DB4, Raspberry_Pi_1.GPIO22
  N10: LCD1.DB5, Raspberry_Pi_1.GPIO27
  N11: LCD1.DB6, Raspberry_Pi_1.GPIO4
  N12: LCD1.DB7, Raspberry_Pi_1.GPIO17
